// Logisim project 4 - BIT RIPPLE DOWN COUNTER.circ as structural Verilog: 1 circuit, main circuit main
module main (
);

  wire button_1_out, CLOCK_out, d_ff_1_q, d_ff_1_qn, d_ff_2_q, d_ff_2_qn, d_ff_3_q, d_ff_3_qn, d_ff_4_q,
       d_ff_4_qn;

  Clock CLOCK (.out(CLOCK_out));
  Button button_1 (.out(button_1_out));
  D_Flip_Flop d_ff_1 (
    .clk(CLOCK_out), .D(d_ff_1_qn), .Q(d_ff_1_q), .Qn(d_ff_1_qn), .reset(button_1_out));  // open: preset
  LED led_1 (.in(d_ff_1_q));
  LED led_2 (.in(d_ff_2_q));
  D_Flip_Flop d_ff_2 (
    .clk(d_ff_1_q), .D(d_ff_2_qn), .Q(d_ff_2_q), .Qn(d_ff_2_qn), .reset(button_1_out));  // open: preset
  D_Flip_Flop d_ff_3 (
    .clk(d_ff_2_q), .D(d_ff_3_qn), .Q(d_ff_3_q), .Qn(d_ff_3_qn), .reset(button_1_out));  // open: preset
  LED led_3 (.in(d_ff_3_q));
  LED led_4 (.in(d_ff_4_q));
  D_Flip_Flop d_ff_4 (
    .clk(d_ff_3_q), .D(d_ff_4_qn), .Q(d_ff_4_q), .Qn(d_ff_4_qn), .reset(button_1_out));  // open: preset

  // Notes on the sheet:
  //   RESET
  //   D0
  //   4 - BIT RIPPLE DOWN COUNTER
  //   D1
  //   D2
  //   D3
endmodule
