// Logisim project 2 BIT ALU.circ as structural Verilog: 1 circuit, main circuit main
module main (
  input  [1:0] A,
  input  [1:0] B,
  input  [2:0] MULTIPLEXER_BITS,
  output [1:0] OUTPUT
);

  wire [1:0] adder_1_out, divider_1_out, multiplier_1_out, subtractor_1_out;

  Adder #(.width(2)) adder_1 (.a(A), .b(B), .out(adder_1_out));  // open: cin, cout
  Subtractor #(.width(2)) subtractor_1 (.a(A), .b(B), .out(subtractor_1_out));  // open: bin, bout
  Multiplier #(.width(2)) multiplier_1 (.a(A), .b(B), .out(multiplier_1_out));  // open: cin, cout
  Divider #(.width(2)) divider_1 (.a(A), .b(B), .out(divider_1_out));  // open: upper, rem
  Multiplexer #(.select(3), .width(2)) multiplexer_1 (
    .in0(adder_1_out), .in1(subtractor_1_out), .in2(multiplier_1_out), .in3(divider_1_out), .out(OUTPUT),
    .sel(MULTIPLEXER_BITS));  // open: in4, in5, in6, in7, en

  // Notes on the sheet:
  //   ADDER
  //   SUBTRACTOR
  //   DIVIDER
  //   2 -  BIT ARITHMETIC LOGIC UNIT
  //   MULTIPLIER
  //   8:1 MULTIPLEXER
endmodule
