// Logisim project D - FLIP FLOP USING NAND GATES.circ as structural Verilog: 1 circuit, main circuit main
module main (
  input  D
);

  wire CLOCK_out, NAND_2_out, NAND_3_out, NAND_4_out, NAND_out, not_1_out;

  Clock CLOCK (.out(CLOCK_out));
  not not_1 (not_1_out, D);
  nand NAND (NAND_out, NAND_4_out, D, CLOCK_out);
  nand NAND_2 (NAND_2_out, CLOCK_out, not_1_out, NAND_3_out);
  nand NAND_3 (NAND_3_out, NAND_out, NAND_4_out);
  nand NAND_4 (NAND_4_out, NAND_3_out, NAND_2_out);
  LED led_1 (.in(NAND_3_out));
  LED led_2 (.in(NAND_4_out));

  // Notes on the sheet:
  //   D - FLIP FLOP USING NAND GATES
  //   Q
  //   Q'
endmodule
