// Logisim project Full Adder.circ as structural Verilog: 1 circuit, main circuit main
module main (
  input  A,
  input  B,
  input  C,
  output SUM,
  output CARRY
);

  wire AND_2_out, AND_out, XOR_out;

  xor XOR (XOR_out, B, C);
  and AND (AND_out, C, B);
  xor XOR_2 (SUM, A, XOR_out);
  and AND_2 (AND_2_out, XOR_out, A);
  or OR (CARRY, AND_2_out, AND_out);

  // Notes on the sheet:
  //   Full - Adder
endmodule
