// Logisim project Half Adder.circ as structural Verilog: 1 circuit, main circuit main
module main (
  input  A,
  input  B,
  output SUM,
  output CARRY
);

  xor XOR (SUM, A, B);
  and AND (CARRY, B, A);

  // Notes on the sheet:
  //   Half - Adder
endmodule
