// Logisim project 4-1 DEMUX.circ as structural Verilog: 1 circuit, main circuit main
module main (
  input  INPUT,
  input  S1,
  input  S0,
  output Y0,
  output Y1,
  output Y2,
  output Y3
);

  wire not_1_out, not_2_out;

  not not_1 (not_1_out, S1);
  not not_2 (not_2_out, S0);
  and AND (Y0, not_1_out, not_2_out, INPUT);
  and AND_2 (Y1, not_1_out, S0, INPUT);
  and AND_3 (Y2, S1, not_2_out, INPUT);
  and AND_4 (Y3, S1, S0, INPUT);

  // Notes on the sheet:
  //   4 : 1 DEMULTIPLEXER
endmodule
