// Logisim project 4 - BIT SERIAL IN SERIAL OUT SHIFT REGISTER.circ as structural Verilog: 1 circuit, main circuit main
module main (
  input  SERIAL_INPUT
);

  wire button_1_out, CLOCK_out, d_ff_1_q, d_ff_2_q, d_ff_3_q, d_ff_4_q;

  Clock CLOCK (.out(CLOCK_out));
  Button button_1 (.out(button_1_out));
  D_Flip_Flop d_ff_1 (.clk(CLOCK_out), .D(SERIAL_INPUT), .Q(d_ff_1_q), .reset(button_1_out));  // open: Qn, preset
  D_Flip_Flop d_ff_2 (.clk(CLOCK_out), .D(d_ff_1_q), .Q(d_ff_2_q), .reset(button_1_out));  // open: Qn, preset
  D_Flip_Flop d_ff_3 (.clk(CLOCK_out), .D(d_ff_2_q), .Q(d_ff_3_q), .reset(button_1_out));  // open: Qn, preset
  D_Flip_Flop d_ff_4 (.clk(CLOCK_out), .D(d_ff_3_q), .Q(d_ff_4_q), .reset(button_1_out));  // open: Qn, preset
  LED led_1 (.in(d_ff_4_q));

  // Notes on the sheet:
  //   RESET  
  //   4 - BIT SERIAL IN SERIAL OUT SHIFT REGISTER
  //   SERIAL OUTPUT
endmodule
