// Logisim project Parallel IN Parallel OUT.circ as structural Verilog: 1 circuit, main circuit main
module main (
  input  D3,
  input  D2,
  input  D1,
  input  D0
);

  wire clock_1_out, d_ff_1_q, d_ff_2_q, d_ff_3_q, d_ff_4_q;

  Clock clock_1 (.out(clock_1_out));
  D_Flip_Flop d_ff_1 (.clk(clock_1_out), .D(D3), .Q(d_ff_1_q));  // open: Qn, preset, reset
  LED led_1 (.in(d_ff_1_q));
  D_Flip_Flop d_ff_2 (.clk(clock_1_out), .D(D2), .Q(d_ff_2_q));  // open: Qn, preset, reset
  LED led_2 (.in(d_ff_2_q));
  D_Flip_Flop d_ff_3 (.clk(clock_1_out), .D(D1), .Q(d_ff_3_q));  // open: Qn, preset, reset
  LED led_3 (.in(d_ff_3_q));
  D_Flip_Flop d_ff_4 (.clk(clock_1_out), .D(D0), .Q(d_ff_4_q));  // open: Qn, preset, reset
  LED led_4 (.in(d_ff_4_q));

  // Notes on the sheet:
  //   Clock
  //   Q3
  //   4 - BIT PARALLEL IN PARALLEL OUT SHIFT REGISTER
  //   Q2
  //   Q2
  //   Q1
  //   Q0
endmodule
