// Logisim project Commutative Property.circ as structural Verilog: 1 circuit, main circuit main
module main (
  input  A,
  input  B,
  input  B_2,
  input  A_2,
  output A___B,
  output B___A
);

  or OR (A___B, A, B_2);
  or OR_2 (B___A, B, A_2);

  // Notes on the sheet:
  //   LHS
  //   Commutative Property
  //   =
  //   RHS
endmodule
