// Logisim project Demorgan's Second Theorem.circ as structural Verilog: 1 circuit, main circuit main
module main (
  input  A,
  input  A_2,
  input  B,
  input  B_2,
  output A_B__prime,
  output A_prime___B_prime
);

  wire not_1_out, not_2_out;

  nor NOR (A_B__prime, A, B);
  not not_1 (not_1_out, A_2);
  not not_2 (not_2_out, B_2);
  and AND (A_prime___B_prime, not_1_out, not_2_out);

  // Notes on the sheet:
  //   LHS
  //   Demorgan's Second Theorem
  //   =
  //   RHS
endmodule
